# Fritzing sketch study space wiring (saved by Fritzing 1.0.6)
breadboards: 1

parts:
  R1 = Resistor [tolerance=±5% resistance=470 package="0805 [SMD]"]
  LCD2 = TFT 1.8 inch 160x128 w SD
  Part1 = 24 NeoPixel Ring [part_number=1586]
  Mod1 = Arduino MKR Wifi 1010
  RE1 = KY-040 Rotary encoder [package="Breakout board"]

nets:
  N1: R1.Pin_0, Mod1.D1
  N2: R1.Pin_1, Part1.IN
  VDD: LCD2.pin_1, LCD2.pin_8, Part1.VDD, Mod1.+5V, RE1.Vcc
  GND: LCD2.pin2, Part1.GND, Mod1.GND, RE1.GND
  N3: LCD2.pin3, Mod1.~D5
  N4: LCD2.pin4, Mod1.D6
  N5: LCD2.pin_5, Mod1.D7
  N6: LCD2.pin_6, Mod1.D8/MOSI
  N7: LCD2.pin_7, Mod1.D9/SCK
  N8: Mod1.~D2, RE1.CLK
  N9: Mod1.~D3, RE1.DT
  N10: Mod1.~D4, RE1.SW

custom parts:
  TFT 1.8 inch 160x128 w SD: This is a generic 1.8 tft spi lcd display available on ebay and others. The 1.8" display has 128x160 color pixels and in this version pin names in breadboard (unlike the real board).
  24 NeoPixel Ring: 24 ultra bright smart LED NeoPixels are arranged in a circle with 2.6" (66mm) outer diameter. The rings are 'chainable' - connect the output pin of one to the input pin of another. Use only one microcontroller pin to control as many as you can chain together! Each LED is addressable as the driver chip is inside the LED. Each one has ~18mA constant current drive so the color will be very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
  Arduino MKR Wifi 1010: Arduino MKR Wifi 1010, SAMD21 Cortex-M0+ 32bit Low Power ARM MCU,Flash Memory 256 KB, SRAM 32KB, 48mhz clock, Ublok Wifi interface.
  KY-040 Rotary encoder: KY-040 Rotary Encoder with switch on breakout borad from AZ Delivery
